# Fritzing sketch connection (saved by Fritzing 0.9.3b)
circuit board: 8.46667cm x 5.64444cm

parts:
  Часть1 = Arduino Nano (Rev3.0)
  Часть2 = Bluetooth HC-05 Macho
  Часть3 = Adafruit DS1307 RTC Breakout [part_number="Adafruit #264"]

nets (from the schematic view):
  N1: Часть1.D1/TX, Часть2.RXD
  N2: Часть1.D0/RX, Часть2.TXD
  GND: Часть1.GND, Часть2.GND, Часть3.GND
  VCC: Часть1.5V, Часть2.VCC, Часть3.VCC
  N3: Часть1.A5, Часть3.SCL
  N4: Часть1.A4, Часть3.SDA

custom parts:
  Adafruit DS1307 RTC Breakout: This is a great battery-backed real time clock (RTC) that allows your microcontroller project to keep track of time even if it is reprogrammed, or if the power is lost. Perfect for datalogging, clock-building, time stamping, timers and alarms, etc. The DS1307 is the most popular RTC - but it requires 5V power to work (although we've used it with 5V power and 3.3V logic successfully) PCB &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
